# Fritzing sketch fritzing circuit (saved by Fritzing 0.9.4)

parts:
  Part2 = Arduino Uno (Rev3)
  M8 = L293D Motor Driver
  M9 = DC Motor
  M10 = DC Motor
  M11 = DC Motor
  M12 = DC Motor
  BAT2 = BC9VPC [package=bc9vpc]
  HC-SR04_Sensor_2 = HC-SR04 Ultrasonic Distance Sensor
  J1 = Basic Servo

nets:
  N1: Part2.A4/SDA, HC-SR04_Sensor_2.TRIG
  N2: Part2.A5/SCL, HC-SR04_Sensor_2.ECHO
  N3: Part2.D9_PWM, J1.pulse
  N4: Part2.D10_PWM/SS, M8.pin_5
  N5: Part2.D11_PWM/MOSI, M8.pin_6
  N6: Part2.D12/MISO, M8.pin_7
  N7: Part2.D13/SCK, M8.pin_8
  GND: Part2.GND, BAT2.V-, HC-SR04_Sensor_2.GND, J1.gnd
  VCC: Part2.5V, HC-SR04_Sensor_2.VCC, J1.vcc
  N8: Part2.VIN, BAT2.V+
  N9: M8.pin_9, M11.pin_1, M12.pin_1
  N10: M8.pin_10, M11.pin_2, M12.pin_2
  N11: M8.pin_11, M9.pin_1, M10.pin_1
  N12: M8.pin_12, M9.pin_2, M10.pin_2
