# Fritzing sketch fritzing circuit (saved by Fritzing 0.9.4)

parts:
  Part3 = Arduino Uno (Rev3)
  M11 = L293D Motor Driver
  M12 = DC Motor
  M13 = DC Motor
  M14 = DC Motor
  M15 = DC Motor
  BAT3 = BC9VPC [package=bc9vpc]
  HC-SR04_Sensor_1 = HC-SR04 Ultrasonic Distance Sensor
  M16 = fc-51 [package=THT]
  M17 = fc-51 [package=THT]

nets:
  N1: Part3.A3, M16.pin1
  N2: Part3.A4/SDA, M17.pin1
  N3: Part3.D8, HC-SR04_Sensor_1.TRIG
  N4: Part3.D9_PWM, M11.pin_5
  N5: Part3.D10_PWM/SS, M11.pin_6
  N6: Part3.D11_PWM/MOSI, M11.pin_7
  N7: Part3.D12/MISO, M11.pin_8
  N8: Part3.D7, HC-SR04_Sensor_1.ECHO
  N9: Part3.5V, M17.pin3
  N10: Part3.GND, BAT3.V-, M17.pin2
  N11: Part3.VIN, BAT3.V+
  N12: M11.pin_9, M14.pin_1, M15.pin_1
  N13: M11.pin_10, M14.pin_2, M15.pin_2
  N14: M11.pin_11, M12.pin_1, M13.pin_1
  N15: M11.pin_12, M12.pin_2, M13.pin_2
  N16: HC-SR04_Sensor_1.VCC, M16.pin3
  N17: HC-SR04_Sensor_1.GND, M16.pin2
